# Fritzing sketch LED Configuration System (saved by Fritzing 0.9.3b)
breadboards: 1

parts:
  LED1 = LED - 5mm [color="Green (565nm)" package="5 mm [THT]"]
  Part2 = Arduino Uno (Rev3)
  U2 = LCD-16X2 [package=lcd-16x2]
  R1 = Resistor [tolerance=±20% resistance=150 package=THT]
  R2 = Trimmer Potentiometer [maximum_resistance=10kΩ package=THT]
  R3 = Resistor [tolerance=±5% resistance=220 package="2010 [SMD]"]

nets:
  N1: LED1.cathode, Part2.GND, R2.leg1
  N2: LED1.anode, Part2.A0, R1.Pin_1
  N3: Part2.D2, U2.DB7, U2.A
  N4: Part2.D3_PWM, U2.DB6
  N5: Part2.D4, U2.DB5
  N6: Part2.D5_PWM, U2.DB3, U2.DB4
  N7: Part2.5V, R1.Pin_0, R2.leg2, R3.Pin_0
